# Fritzing sketch circuit_all_sensors_arduino (saved by Fritzing 0.9.3b)
breadboards: 1

parts:
  R1 = Resistor [tolerance=±5% resistance=2k package=THT]
  DHT2 = DHT22 Humidity and Temperature Sensor
  Componente1 = Arduino Uno (Rev3)
  DHT11_Variante_1 = DHT11 Humitidy and Temperature Sensor
  DHT11_Variante_2 = DHT11 Humitidy and Temperature Sensor
  LM35 = LM35 Temperature Sensor [package="TO92 [THT]"]
  LM335 = LM335 Temperature Sensor [package="DIP (Dual Inline)"]
  DS18B20 = DS18B20 1-Wire Temperature Sensor [part_number=DS18B20]
  TMP36 = TMP36 Temperature Sensor [package="TO92 [THT]"]
  Componente2 = Real Time Clock Module - DS1307 RTC Breakout Board

nets:
  N1: R1.Pin_0, Componente1.A1, LM335.Positive_V_+
  VDD: R1.Pin_1, DHT2.VDD, Componente1.5V, DHT11_Variante_1.VDD, DHT11_Variante_2.VDD, LM35.+Vs, DS18B20.VDD, TMP36.+Vs, Componente2.5V
  N2: DHT2.DATA, Componente1.D5_PWM
  GND: DHT2.GND, Componente1.GND, DHT11_Variante_1.GND, DHT11_Variante_2.GND, LM35.GND, LM335.Negative_V_-, DS18B20.GND, TMP36.GND, Componente2.GND
  N3: Componente1.A0, LM35.Vout
  N4: Componente1.A2, TMP36.Vout
  N5: Componente1.D8, Componente2.SCL
  N6: Componente1.D9_PWM, Componente2.SQW
  N7: Componente1.D2, Componente2.SDA
  N8: Componente1.D4, DS18B20.DQ
  N9: Componente1.D6_PWM, DHT11_Variante_2.DATA
  N10: Componente1.D7, DHT11_Variante_1.DATA

notes:
  Analog
  Digital - PWM
  irwinet

custom parts:
  DHT11 Humitidy and Temperature Sensor: DHT11 Humidity and Temperature Sensor
  LM335 Temperature Sensor: A DIP stand-in part for whatever IC you want. With 4 pins on a 300 mil dual inline package (DIP) footprint.
