# Fritzing sketch circuit_dht11_variant1 (saved by Fritzing 0.9.3b)
breadboards: 1

parts:
  Mod1 = Raspberry Pi 4B
  DHT1 = DHT11 Humitidy and Temperature Sensor
  R1 = Resistor [tolerance=±5% resistance=10k package=THT]

nets:
  5V: Mod1.5V, DHT1.VDD, R1.Pin_0
  N1: Mod1.GPIO4, DHT1.DATA, R1.Pin_1
  GND: Mod1.GND, DHT1.GND

notes:
  PIN 1
  3V
  PIN 2
  5V
  irwinet

custom parts:
  DHT11 Humitidy and Temperature Sensor: DHT11 Humidity and Temperature Sensor
