# Fritzing sketch circuit_dht22 (saved by Fritzing 0.9.3b)
breadboards: 1

parts:
  Mod1 = Raspberry Pi 4B
  R1 = Resistor [tolerance=±5% resistance=10k package=THT]
  DHT2 = DHT22 Humidity and Temperature Sensor

nets:
  5V: Mod1.5V, R1.Pin_0, DHT2.VDD
  N1: Mod1.GPIO4, R1.Pin_1, DHT2.DATA
  GND: Mod1.GND, DHT2.GND

notes:
  PIN 1
  3V
  PIN 2
  5V
  irwinet
