# Fritzing sketch circuit_lm35_mcp3008 (saved by Fritzing 0.9.3b)
breadboards: 1

parts:
  Mod1 = Raspberry Pi 4B
  IC1 = MCP3008 8-channel 10-bit ADC [part_number=MCP3008]
  R1 = Resistor [tolerance=±5% resistance=470 package=THT]
  R2 = Resistor [tolerance=±5% resistance=1k package=THT]
  T2 = LM35 Temperature Sensor [package="TO92 [THT]"]

nets:
  N1: Mod1.3V3, IC1.no_name_yet#15, IC1.no_name_yet#16
  N2: Mod1.5V, T2.+Vs
  N3: Mod1.GPIO10, IC1.no_name_yet#11
  N4: Mod1.GPIO9, IC1.no_name_yet#12
  N5: Mod1.GPIO11, IC1.no_name_yet#13
  N6: Mod1.GPIO8, IC1.no_name_yet#10
  N7: IC1.no_name_yet#1, R2.Pin_0, T2.Vout
  N8: IC1.no_name_yet#9, IC1.no_name_yet#14, R1.Pin_0, T2.GND
  N9: R1.Pin_1, R2.Pin_1

notes:
  PIN 1
  3V
  PIN 2
  5V
  irwinet
