# Fritzing sketch pcb_raspberrypi (saved by Fritzing 0.9.3b)
breadboards: 1

parts:
  Mod1 = Raspberry Pi 4B
  M1 = DC Motor
  LED1 = LED - 3mm [color="Red (633nm)" package="3 mm [THT]"]
  R1 = Resistor [tolerance=±5% resistance=330 package=THT]
  RHT1 = Humidity and Temperature Sensor RHT03
  RHT2 = Humidity and Temperature Sensor RHT03
  M2 = DC Motor

nets:
  VCC: Mod1.5V, RHT1.Vcc, RHT2.Vcc
  N1: Mod1.GND, Mod1.GPIO14, M1.pin_2, LED1.cathode, RHT1.GND_1, RHT2.GND_1, M2.pin_2
  N2: Mod1.GPIO4, R1.Pin_0
  N3: LED1.anode, R1.Pin_1

notes:
  12V
  -
  +
  DHT1
  DHT2
